# Fritzing sketch Stairway proto (saved by Fritzing 0.9.2b)

parts:
  Q1 = Basic FET N-Channel [package="TO220 [THT]"]
  Q2 = Basic FET N-Channel [package="TO220 [THT]"]
  Q3 = Basic FET N-Channel [package="TO220 [THT]"]
  V1 = DC Power [voltage=12V]
  R1 = Resistor [tolerance=±5% resistance=10k package=THT]
  R2 = Resistor [tolerance=±5% resistance=10k package=THT]
  R3 = Resistor [tolerance=±5% resistance=10k package=THT]
  R4 = Photocell (LDR) [package=THT]
  R5 = Resistor [tolerance=±5% resistance=10k package=THT]
  R6 = Photocell (LDR) [package=THT]
  R7 = Resistor [tolerance=±5% resistance=10k package=THT]
  R8 = Photocell (LDR) [package=THT]
  R9 = Resistor [tolerance=±5% resistance=10k package=THT]
  R10 = Photocell (LDR) [package=THT]
  R11 = Photocell (LDR) [package=THT]
  R12 = Photocell (LDR) [package=THT]
  R13 = Resistor [tolerance=±5% resistance=10k package=THT]
  R14 = Resistor [tolerance=±5% resistance=10k package=THT]
  R15 = Resistor [tolerance=±5% resistance=10k package=THT]
  Part1 = Arduino Uno (Rev3)
  J1 = Infrared Proximity Sensor
  U1 = mystery part, 7 pins [chip_label=MB1040]
  Reset = Pushbutton [package="[THT]"]
  R16 = Resistor [tolerance=±20% resistance=10k package=THT]
  S1 = Pushbutton [package="[THT]"]
  R17 = Resistor [tolerance=±5% resistance=10k package=THT]
  Part2 = Analog Digital MUX Breakout
  C1 = Electrolytic Capacitor [capacitance=10µF package="100 mil [THT, electrolytic]"]
  J2 = Infrared Proximity Sensor
  C2 = Electrolytic Capacitor [capacitance=10µF package="100 mil [THT, electrolytic]"]

nets:
  N1: Q1.gate, R1.Pin_1, Part1.D3_PWM
  LED Strip -: Q1.drain, Q2.drain, Q3.drain
  GND: Q1.source, Q2.source, Q3.source, V1.V-, R1.Pin_0, R2.Pin_0, R3.Pin_0, R5.Pin_0, R7.Pin_0, R9.Pin_0, R13.Pin_0, R14.Pin_0, R15.Pin_0, Part1.GND, J1.GND, U1.pin1, R16.Pin_0, R17.Pin_0, Part2.GND, C1.-
  N2: Q2.gate, R2.Pin_1, Part1.D5_PWM
  N3: Q3.gate, R3.Pin_1, Part1.D6_PWM
  LED Strip +: V1.V+, Part1.VIN
  N4: R4.pin_0, R5.Pin_1, Part2.C0
  VCC: R4.pin_1, R6.pin_1, R8.pin_1, R10.pin_1, R11.pin_1, R12.pin_1, Part1.5V, J1.Vcc, Reset.Pin_1, Reset.Pin_2, C1.+, J2.Vcc, C2.+
  N5: R6.pin_0, R7.Pin_1, Part2.C1
  N6: R8.pin_0, R9.Pin_1, Part2.C2
  N7: R10.pin_0, R13.Pin_1, Part2.C5
  N8: R11.pin_0, R14.Pin_1, Part2.C4
  N9: R12.pin_0, R15.Pin_1, Part2.C3
  N10: Part1.D10_PWM/SS, U1.pin6
  N11: Part1.D11_PWM/MOSI, S1.Pin_3, S1.Pin_4, R17.Pin_1
  N12: Part1.RESET, Reset.Pin_3, Reset.Pin_4, R16.Pin_1
  N13: J1.Vout, Part2.C6
  N14: U1.pin2, S1.Pin_1, S1.Pin_2, Part2.VCC
  N15: Part2.C7, J2.Vout
  N16: J2.GND, C2.-
